# Fritzing sketch module.schematic (saved by Fritzing 0.9.3b)
breadboards: 1

parts:
  Part1 = Arduino Uno (Rev3)
  U1 = ESP8266 WiFi Module [part_number=ESP8266]
  R1 = Resistor [tolerance=±5% resistance=10k package=THT]
  R2 = Resistor [tolerance=±5% resistance=20k package=THT]
  IC1 = Voltage Regulator LM1117 [package=sot223]
  Part2 = RFID USB Reader

nets:
  GND: Part1.GND, U1.GND, R2.Pin_0, IC1.ADJ, Part2.GND
  N1: Part1.D2, U1.TXD
  N2: Part1.D3_PWM, R1.Pin_0
  N3: Part1.D5_PWM, Part2.TX-O-RS232
  N4: Part1.D6_PWM, Part2.TX-O
  5V: Part1.5V, IC1.IN, Part2.VCC
  N5: U1.RXD, R1.Pin_1, R2.Pin_1
  N6: U1.VCC, IC1.OUT
